# Fritzing sketch esp32-1-kap1-esp32-devkit-steckbrett (saved by Fritzing 1.0.0rc)
breadboards: 2

parts:
  R2 = Resistor [tolerance=±5% resistance=1k power=0.25W package=THT]
  LED1 = LED - 5mm [color="Red (633nm)" current=0.030A package="5 mm [THT]"]
  M1 = DOIT Esp32 DevKit v1 (30 pins long, 11 pins width) [part_number=ESP32S-PIN30]

nets:
  N1: R2.Pin_0, M1.D4
  N2: R2.Pin_1, LED1.anode
  N3: LED1.cathode, M1.GND

custom parts:
  DOIT Esp32 DevKit v1 (30 pins long, 11 pins width): The DOIT Esp32 DevKit v1 is one of the development board created by DOIT to evaluate the ESP-WROOM-32 module. It is based on the ESP32 microcontroller that boasts Wifi, Bluetooth, Ethernet and Low Power support all in a single chip. (vanepp) made breadboard work, adjusted pin numbering and labels and reduced size of schematic and cleaned up pcb. This chip is 30pins long (2 x15) and 11 pins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
