# Fritzing sketch esp32-1-kap5-esp32-xiao-if-gpio-steckbrett (saved by Fritzing 1.0.0rc)
breadboards: 1

parts:
  R2 = Resistor [tolerance=±5% resistance=1k power=0.25W package=THT]
  A1 = XIAO ESP32C3-smd
  LED1 = LED - 5mm [color="Red (633nm)" current=0.030A package="5 mm [THT]"]
  S1 = Pushbutton [package="[SMD]"]

nets:
  N1: R2.Pin_0, LED1.anode
  N2: R2.Pin_1, A1.Pin_11
  N3: A1.Pin_2, A1.Pin_21, LED1.cathode
  N4: A1.Pin_9, S1.Pin_1, S1.Pin_2
  N5: A1.Pin_20, S1.Pin_3, S1.Pin_4

custom parts:
  XIAO ESP32C3-smd: Seeed Studio XIAO ESP32C3 adopts new RISC-V architecture, supporting both Wi-Fi and BLE wireless connectivities.
