# Fritzing sketch esp32-1-kap6-esp32-xiao-analog-ausgang (saved by Fritzing 1.0.0rc)
breadboards: 1

parts:
  A1 = XIAO ESP32C3-smd
  R1 = Resistor [tolerance=±5% power=0.25W resistance=10k package=THT]
  C1 = Ceramic Capacitor [capacitance=100nF voltage=35V package="100 mil [THT, multilayer]"]
  VM1 = Multimeter (DC Voltage)

nets:
  N1: A1.Pin_2, A1.Pin_21, C1.1, VM1.COM_Probe
  N2: A1.Pin_19, R1.Pin_0
  N3: R1.Pin_1, C1.0, VM1.V_Probe

custom parts:
  XIAO ESP32C3-smd: Seeed Studio XIAO ESP32C3 adopts new RISC-V architecture, supporting both Wi-Fi and BLE wireless connectivities.
