# Fritzing sketch esp32-1-kap6-esp32-xiao-analog-eingang-steckbrett (saved by Fritzing 1.0.0rc)
breadboards: 1

parts:
  A1 = XIAO ESP32C3-smd
  U1 = POT [knob_status=50% power=0.5W package=pot_mammoth]

nets:
  N1: A1.Pin_11, U1.A
  N2: A1.Pin_20, U1.S
  N3: A1.Pin_21, U1.E

custom parts:
  XIAO ESP32C3-smd: Seeed Studio XIAO ESP32C3 adopts new RISC-V architecture, supporting both Wi-Fi and BLE wireless connectivities.
