# Fritzing sketch esp32-1-kap6-esp32-xiao-spi-max31865-steckbrett (saved by Fritzing 1.0.0rc)
breadboards: 1

parts:
  A1 = XIAO ESP32C3-smd
  Bauteil1 = Adafruit MAX31865 RTD Sensor Breakout [part_number="Adafruit #3328"]

nets:
  N1: A1.Pin_16, Bauteil1.CS
  N2: A1.Pin_17, Bauteil1.SCLK
  N3: A1.Pin_18, Bauteil1.SDO
  N4: A1.Pin_19, Bauteil1.SDI
  N5: A1.Pin_21, Bauteil1.GND
  N6: A1.Pin_22, Bauteil1.VIN

custom parts:
  XIAO ESP32C3-smd: Seeed Studio XIAO ESP32C3 adopts new RISC-V architecture, supporting both Wi-Fi and BLE wireless connectivities.
  Adafruit MAX31865 RTD Sensor Breakout: For precision temperature sensing, nothing beats a Platinum RTD. Resistance temperature detectors (RTDs) are temperature sensors that contain a resistor that changes resistance value as its temperature changes, basically a kind of thermistor. In this sensor, the resistor is actually a small strip of Platinum with a resistance of 100 ohms at 0°C, thus the name PT100. Compared to most NTC/PTC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
